# Fritzing sketch Temp-LDR-Circuit (saved by Fritzing 0.5.2b)
breadboards: 1

parts:
  R1 = Resistor [resistance=10k package=THT]
  R2 = Photocell (LDR) [package=THT]
  Q1 = NPN-Transistor [package="TO92 [THT]"]
  Arduino1 = Arduino

nets:
  N1: R1.Pin_0, R2.pin_1, Arduino1.A0
  N2: R1.Pin_1, Q1.C, Arduino1.GND
  N3: R2.pin_0, Q1.E, Arduino1.+5V
  N4: Q1.B, Arduino1.A1
